// Logisim project IOcircut.circ as structural Verilog: 1 circuit, main circuit main
module main (
  output out_1
);

  wire and_1_out, and_2_out, and_3_out, Ausgabewert_q, Clock, controlled_buffer_1_out, Eingabewert_q,
       not_1_out, Richtung_q, undriven, undriven_2, undriven_4, undriven_5;
  wire [1:0] undriven_3;

  assign controlled_buffer_1_out = undriven_3[0] ? Eingabewert_q : 1'bz;  // Controlled_Buffer controlled_buffer_1
  and and_1 (and_1_out, undriven_4, Clock);
  D_Flip_Flop Richtung (.clk(and_1_out), .D(undriven), .Q(Richtung_q));  // open: Qn, preset, en, reset
  and and_2 (and_2_out, undriven_3[1], Clock);
  D_Flip_Flop Ausgabewert (.clk(and_2_out), .D(undriven_2), .Q(Ausgabewert_q));  // open: Qn, preset, en, reset
  not not_1 (not_1_out, Richtung_q);
  assign out_1 = not_1_out ? Ausgabewert_q : 1'bz;  // Controlled_Buffer controlled_buffer_2
  and and_3 (and_3_out, undriven_5, Clock);
  D_Flip_Flop Eingabewert (.clk(and_3_out), .D(out_1), .Q(Eingabewert_q));  // open: Qn, preset, en, reset

  // Notes on the sheet:
  //   Datenbus
  //   Richtung
  //   Ausgabewert
  //   Eingabewert
  //   Systembus
endmodule
